# Fritzing sketch airqual (saved by Fritzing 0.9.3b)
breadboards: 1

parts:
  WeMos_D1_Mini1 = WeMos D1 Mini
  R2 = Resistor [tolerance=±5% resistance=10k package="2512 [SMD]"]
  Bauteil1 = Adafruit CCS811
  DHT1 = DHT22 Humidity and Temperature Sensor

nets:
  3V3: WeMos_D1_Mini1.3V3, R2.Pin_1, Bauteil1.VIN, DHT1.VDD
  N1: WeMos_D1_Mini1.G, Bauteil1.GND, Bauteil1.!WAKE
  N2: R2.Pin_0, DHT1.DATA
