# Fritzing sketch doc (saved by Fritzing 0.9.3b)
breadboards: 1

parts:
  WeMos_D1_Mini1 = WeMos D1 Mini  # not connected
  LED1 = LED - 5mm [color="Red (633nm)" package="5 mm [THT]"]
  R1 = Resistor [tolerance=±5% resistance=330 package="0805 [SMD]"]
  S1 = Round Pushbutton  # not connected

nets:
  N1: LED1.anode, R1.Pin_0
